# Fritzing sketch circuit (saved by Fritzing 0.9.3b)

parts:
  J1 = STM32 Nucleo boards
  R1 = Resistor [tolerance=±5% resistance=22 package=THT]
  SP1 = SPEAKER [package=pcb_mount_speaker]
  SP2 = SPEAKER [package=pcb_mount_speaker]
  R3 = Resistor [tolerance=±5% resistance=22 package=THT]
  SP3 = SPEAKER [package=pcb_mount_speaker]
  R4 = Resistor [tolerance=±5% resistance=22 package=THT]

nets:
  N1: J1.PA13, R1.Pin_0
  N2: J1.PC14, R4.Pin_0
  N3: J1.PC2, R3.Pin_0
  N4: J1.PC3, SP1.+, SP2.+, SP3.+
  N5: R1.Pin_1, SP1.-
  N6: SP2.-, R4.Pin_1
  N7: R3.Pin_1, SP3.-

notes:
  GND
  PA4
  PB3
  PB4
  22Ω
