# Fritzing sketch circuit_single_speaker (saved by Fritzing 0.9.3b)

parts:
  J1 = STM32 Nucleo boards
  SP1 = SPEAKER [package=pcb_mount_speaker]
  R3 = Resistor [tolerance=±5% resistance=22 package=THT]
  R1 = Resistor [tolerance=±5% resistance=22 package=THT]
  R4 = Resistor [tolerance=±5% resistance=22 package=THT]

nets:
  N1: J1.PA13, R1.Pin_0
  N2: J1.PC14, R4.Pin_0
  N3: J1.PC2, R3.Pin_0
  N4: J1.PC3, SP1.+
  N5: SP1.-, R1.Pin_1, R4.Pin_1

notes:
  GND
  PA4
  PB3
  PB4
  22Ω
